# Fritzing sketch Remote controller (saved by Fritzing 0.9.3b)
breadboards: 1

parts:
  Part1 = Arduino Pro Mini (5V)
  Squix3 = OLED 0.96" 128x64 I2C SSD1306
  S1 = Pushbutton [package="[THT]"]
  S2 = Pushbutton [package="[THT]"]
  S3 = Pushbutton [package="[THT]"]
  S4 = Pushbutton [package="[THT]"]
  S5 = Pushbutton [package="[THT]"]
  Tx1 = mystery part, 3 pins [chip_label=?]
  Arduino_CNC_Shield_V3_00_1 = Arduino_CNC_V3.00
  Rx1 = mystery part, 4 pins [chip_label=?]

nets:
  N1: Part1.A4, Squix3.SCA
  N2: Part1.A5, Squix3.SCL
  GND: Part1.GND, Squix3.GND, S1.Pin_3, S1.Pin_4, S2.Pin_1, S2.Pin_2, S3.Pin_1, S3.Pin_2, S4.Pin_1, S4.Pin_2, S5.Pin_1, S5.Pin_2, Tx1.pin3
  VCC: Part1.VCC, Squix3.VCC, Tx1.pin2
  N3: Part1.MISO, Tx1.pin1
  N4: Part1.D8, S4.Pin_3, S4.Pin_4
  N5: Part1.D7, S5.Pin_3, S5.Pin_4
  N6: Part1.D6, S3.Pin_3, S3.Pin_4
  N7: Part1.D5, S2.Pin_3, S2.Pin_4
  N8: Part1.D4, S1.Pin_1, S1.Pin_2
  N9: Arduino_CNC_Shield_V3_00_1.5V, Rx1.pin1
  N10: Arduino_CNC_Shield_V3_00_1.GND, Rx1.pin4
  N11: Arduino_CNC_Shield_V3_00_1.SpnEn_/_Z_Limit, Rx1.pin3

notes:
  set/up & down
  Home/stop
  Transmitter
  To power bank module

custom parts:
  Arduino_CNC_V3.00: Protoneer Arduino CNC Shield V3.00 If using Grbl V0.9: The “A” axis can not be used (yet). The “SCL” (Arduino A5) pin is now used for 'Probing' input. The “End Stops Z+ & Z-” (Arduino D11) and “SpnEn” (Arduino D12) have been switched!
